// Logisim project trab.circ as structural Verilog: 1 circuit, main circuit main
module main (
  input  [1:0] _2,
  input  in_2,
  input  [7:0] in_3,
  input  in_4,
  input  [1:0] _1,
  input  Reset_Counter,
  input  [1:0] _0,
  input  in_8,
  input  Clear,
  output out_10,
  output [5:0] out_11
);

  wire clock_1_out, not_1_out;
  wire [1:0] bitselector_1_out, bitselector_2_out, bitselector_3_out;
  wire [6:0] undriven;
  wire [7:0] \Percorre_a_Memória_q ;

  Clock clock_1 (.out(clock_1_out));
  Counter #(.ongoal("stay")) \Percorre_a_Memória  (
    .load(in_2), .D(in_3), .count(in_4), .Q(\Percorre_a_Memória_q ), .carry(out_10), .clk(clock_1_out),
    .clr(Reset_Counter));
  not not_1 (not_1_out, out_10);
  ROM #(.dataWidth(6)) rom_1 (.addr(\Percorre_a_Memória_q ), .data(out_11), .sel(not_1_out));
  TTY #(.rows(6), .cols(24)) tty_1 (.data(undriven), .clk(clock_1_out), .we(in_8), .clr(Clear));
  BitSelector #(.width(6), .group(2)) bitselector_1 (.in(out_11), .out(bitselector_1_out), .sel(_2));
  DotMatrix #(.inputtype("row"), .matrixcols(2), .matrixrows(3), .dotshape("circle")) dotmatrix_1 (
    .row0(bitselector_1_out), .row1(bitselector_2_out), .row2(bitselector_3_out));
  BitSelector #(.width(6), .group(2)) bitselector_2 (.in(out_11), .out(bitselector_2_out), .sel(_1));
  BitSelector #(.width(6), .group(2)) bitselector_3 (.in(out_11), .out(bitselector_3_out), .sel(_0));

  // Notes on the sheet:
  //   AQUI
  //   ROM
endmodule
